# Fritzing sketch Charlieplex 2 (saved by Fritzing 0.9.10b)
circuit board: 5.01219cm x 6.97231cm
breadboards: 1

parts:
  LED1 = LED - 5mm [color="Red (633nm)" current=0.030 package="5 mm [THT]"]
  LED2 = LED - 5mm [color="Red (633nm)" current=0.030 package="5 mm [THT]"]
  LED3 = LED - 5mm [color="Red (633nm)" current=0.030 package="5 mm [THT]"]
  LED4 = LED - 5mm [color="Red (633nm)" current=0.030 package="5 mm [THT]"]
  LED8 = LED - 5mm [color="Red (633nm)" current=0.030 package="5 mm [THT]"]
  LED7 = LED - 5mm [color="Red (633nm)" current=0.030 package="5 mm [THT]"]
  LED6 = LED - 5mm [color="Red (633nm)" current=0.030 package="5 mm [THT]"]
  LED5 = LED - 5mm [color="Red (633nm)" current=0.030 package="5 mm [THT]"]
  R2 = Resistor [tolerance=±5% resistance=100 power=0.25 package=THT]
  LED12 = LED - 5mm [color="Red (633nm)" current=0.030 package="5 mm [THT]"]
  LED11 = LED - 5mm [color="Red (633nm)" current=0.030 package="5 mm [THT]"]
  LED10 = LED - 5mm [color="Red (633nm)" current=0.030 package="5 mm [THT]"]
  LED9 = LED - 5mm [color="Red (633nm)" current=0.030 package="5 mm [THT]"]
  R3 = Resistor [tolerance=±5% resistance=100 power=0.25 package=THT]
  LED16 = LED - 5mm [color="Red (633nm)" current=0.030 package="5 mm [THT]"]
  LED15 = LED - 5mm [color="Red (633nm)" current=0.030 package="5 mm [THT]"]
  LED14 = LED - 5mm [color="Red (633nm)" current=0.030 package="5 mm [THT]"]
  LED13 = LED - 5mm [color="Red (633nm)" current=0.030 package="5 mm [THT]"]
  R4 = Resistor [tolerance=±5% resistance=100 power=0.25 package=THT]
  LED20 = LED - 5mm [color="Red (633nm)" current=0.030 package="5 mm [THT]"]
  LED19 = LED - 5mm [color="Red (633nm)" current=0.030 package="5 mm [THT]"]
  LED18 = LED - 5mm [color="Red (633nm)" current=0.030 package="5 mm [THT]"]
  LED17 = LED - 5mm [color="Red (633nm)" current=0.030 package="5 mm [THT]"]
  R5 = Resistor [tolerance=±5% resistance=100 power=0.25 package=THT]
  R1 = Resistor [tolerance=±5% resistance=100 power=0.25 package=THT]
  U1 = attiny85 [package=dip]
  BAT1 = Battery Holders [package=battcom_20mm_pth]

nets (from the schematic view):
  N1: LED1.cathode, LED5.cathode, LED9.cathode, LED13.cathode, LED20.anode, LED19.anode, LED18.anode, LED17.anode, R5.Pin_1
  N2: LED1.anode, LED2.anode, LED3.anode, LED4.anode, LED8.cathode, LED12.cathode, LED16.cathode, LED20.cathode, R1.Pin_1
  N3: LED2.cathode, LED6.cathode, LED10.cathode, LED16.anode, LED15.anode, LED14.anode, LED13.anode, R4.Pin_1, LED17.cathode
  N4: LED3.cathode, LED7.cathode, LED12.anode, LED11.anode, LED10.anode, LED9.anode, R3.Pin_1, LED14.cathode, LED18.cathode
  N5: LED4.cathode, LED8.anode, LED7.anode, LED6.anode, LED5.anode, R2.Pin_1, LED11.cathode, LED15.cathode, LED19.cathode
  N6: R2.Pin_0, U1.Pin_6
  N7: R3.Pin_0, U1.Pin_5
  N8: R4.Pin_0, U1.Pin_2
  N9: R5.Pin_0, U1.Pin_3
  N10: R1.Pin_0, U1.Pin_7
  N11: U1.Pin_4, BAT1.-
  N12: U1.Pin_8, BAT1.+
